# Fritzing sketch Matrix Clock (saved by Fritzing 0.9.10b)
breadboards: 1

parts:
  8x8_LED_Modul_mit_MAX1 = 8x8 LED Modul mit MAX7219 [package=THT]
  R1 = Resistor [tolerance=±5% power=0.25 resistance=10k package=THT]
  S1 = Momentary Switch [package=ksa_sealed_tac_switch]
  RHT1 = Humidity and Temperature Sensor RHT03
  R2 = Resistor [tolerance=±5% power=0.25 resistance=10k package=THT]
  Pico_H1 = Raspberry Pi Pico H

nets:
  N1: 8x8_LED_Modul_mit_MAX1.VCC_Eingang, R1.Pin_0, S1.1, RHT1.Vcc, Pico_H1.VBUS
  N2: 8x8_LED_Modul_mit_MAX1.GND_Eingang, RHT1.GND_2, R2.Pin_0, Pico_H1.GND
  N3: 8x8_LED_Modul_mit_MAX1.DIN_Eingang, Pico_H1.GP0
  N4: 8x8_LED_Modul_mit_MAX1.CS_Eingang, Pico_H1.GP1
  N5: 8x8_LED_Modul_mit_MAX1.CLK_Eingang, Pico_H1.GP2
  N6: R1.Pin_1, RHT1.Data-signal, Pico_H1.GP4
  N7: S1.4, R2.Pin_1, Pico_H1.GP3

custom parts:
  Raspberry Pi Pico H: Raspberry Pi Pico H. Based around the RP2040 microcontroller the Pico H is a low cost microcontroller device bringing Raspberry Pi quality, cost, and easy of use to the microcontroller space.
